# Fritzing sketch bme280-oled (saved by Fritzing 0.9.3b)
breadboards: 1

parts:
  Part1 = BME280 Breakout
  Part2 = Photon
  Squix1 = OLED 0.96" 128x64 I2C SSD1306

nets:
  GND: Part1.GND, Part2.GND, Squix1.GND
  3.3V: Part1.3.3V, Part2.3V3, Squix1.VCC
  N1: Part1.SDI/SDA, Part2.D0, Squix1.SCA
  N2: Part1.SCK/SCL, Part2.D1, Squix1.SCL
